// Digital circuit 000_111_detect.dig as structural Verilog
module _000_111_detect (
  input  Cin,
  input  Ain,
  input  Bin,
  input  I0,
  input  I1,
  input  Int_C,
  output Sum
);

  wire nand_1_out, nand_2_out, nand_3_out, nand_4_out, nand_5_out, nand_6_out, not_1_out, not_2_out,
       not_3_out;

  not not_1 (not_1_out, Ain);
  not not_2 (not_2_out, Bin);
  not not_3 (not_3_out, Cin);
  nand nand_1 (nand_1_out, not_1_out, not_2_out, not_3_out);
  nand nand_2 (nand_2_out, Ain, Bin, Cin);
  nand nand_3 (nand_3_out, nand_1_out, Int_C);
  nand nand_4 (nand_4_out, nand_3_out, nand_2_out);
  nand nand_5 (nand_5_out, nand_4_out, I0);
  nand nand_6 (nand_6_out, I1, Int_C);
  nand nand_7 (Sum, nand_5_out, nand_6_out);

  // Notes on the sheet:
  //   Detect 000
  //   Detect 111
endmodule
