// Digital circuit AOI_bit_serial_ALU.dig as structural Verilog
module AOI_bit_serial_ALU (
  input  Cin,
  input  Ain,
  input  Bin,
  input  I0,
  input  I1,
  input  A_nL,
  input  nInv_B,
  output Carry_Out,
  output Sum,
  output out_10
);

  wire nand_1_out, nand_2_out, nand_3_out, nand_4_out, nand_5_out, nand_7_out, nand_8_out, nand_9_out,
       nand_10_out, nand_11_out, nand_12_out, nand_13_out, nand_14_out, nBin, not_1_out, not_3_out,
       not_4_out, not_5_out;

  not not_1 (not_1_out, Ain);
  not not_2 (nBin, Bin);
  not not_3 (not_3_out, Cin);
  not not_4 (not_4_out, nInv_B);
  nand nand_1 (nand_1_out, Ain, Bin);
  nand nand_2 (nand_2_out, Ain, Cin);
  nand nand_3 (nand_3_out, Bin, Cin);
  nand nand_4 (nand_4_out, nBin, not_4_out);
  nand nand_5 (nand_5_out, nInv_B, Bin);
  nand nand_6 (out_10, nand_4_out, nand_5_out);
  nand nand_7 (nand_7_out, not_1_out, nBin, not_3_out);
  nand nand_8 (nand_8_out, Ain, Bin, Cin);
  nand nand_9 (nand_9_out, nand_1_out, nand_2_out, nand_3_out);
  not not_5 (not_5_out, nand_9_out);
  nand nand_10 (nand_10_out, nand_9_out, A_nL);
  nand nand_11 (nand_11_out, nand_7_out, not_5_out);
  not not_6 (Carry_Out, nand_10_out);
  nand nand_12 (nand_12_out, nand_11_out, nand_8_out);
  nand nand_13 (nand_13_out, nand_12_out, I0);
  nand nand_14 (nand_14_out, I1, not_5_out);
  nand nand_15 (Sum, nand_13_out, nand_14_out);

  // Other names for the same wires on the sheet: Cout = Carry_Out

  // Notes on the sheet:
  //   Detect 000
  //   Detect 111
  //   Suppress Carry
endmodule
