// Digital circuit Z80_single_bit.dig as structural Verilog
module Z80_single_bit (
  input  Cin,
  input  Ain,
  input  Bin,
  input  S,
  input  R,
  input  V,
  output Carry_Out,
  output Function
);

  wire and_1_out, and_2_out, and_3_out, and_4_out, nor_1_out, or_1_out, or_2_out, or_3_out;

  or or_1 (or_1_out, Ain, Bin);
  and and_1 (and_1_out, Cin, or_1_out);
  and and_2 (and_2_out, Ain, Bin);
  nor nor_1 (nor_1_out, and_1_out, and_2_out, S);
  and and_3 (and_3_out, Cin, Ain, Bin);
  or or_2 (or_2_out, Cin, Ain, Bin);
  or or_3 (or_3_out, V, nor_1_out);
  nor nor_2 (Carry_Out, nor_1_out, R);
  and and_4 (and_4_out, or_2_out, or_3_out);
  or or_4 (Function, and_3_out, and_4_out);

  // Notes on the sheet:
  //   Internal ~Cout --->
  //   Z80 single ALU bit
  //   Detect 111
  //   Detect 000
endmodule
