// Digital circuit Z80_style_ALU.dig as structural Verilog
module Z80_style_ALU (
  input  Fn,
  input  Cin,
  input  nB,
  input  nA,
  input  I1,
  input  I0,
  input  Ain,
  input  Bin,
  input  S,
  input  R,
  input  V,
  output Fout,
  output Cout,
  output Carry_Out,
  output Function
);

  wire and_1_out, and_2_out, and_3_out, and_4_out, nand_1_out, nand_2_out, nand_3_out, nand_4_out,
       nand_5_out, nand_6_out, nor_1_out, or_1_out, or_2_out, or_3_out, xor_1_out, xor_2_out, xor_3_out,
       xor_4_out;

  or or_1 (or_1_out, Ain, Bin);
  and and_1 (and_1_out, Cin, or_1_out);
  and and_2 (and_2_out, Ain, Bin);
  xor xor_1 (xor_1_out, Ain, nA);
  xor xor_2 (xor_2_out, nB, Bin);
  nor nor_1 (nor_1_out, and_1_out, and_2_out, S);
  xor xor_3 (xor_3_out, xor_1_out, xor_2_out);
  nor nor_2 (Carry_Out, nor_1_out, R);
  xor xor_4 (xor_4_out, xor_3_out, Cin);
  nand nand_1 (nand_1_out, xor_3_out, Cin);
  nand nand_2 (nand_2_out, xor_1_out, xor_2_out);
  and and_3 (and_3_out, Cin, Ain, Bin);
  or or_2 (or_2_out, Cin, Ain, Bin);
  or or_3 (or_3_out, V, nor_1_out);
  nand nand_3 (nand_3_out, nand_1_out, nand_2_out);
  and and_4 (and_4_out, or_2_out, or_3_out);
  nand nand_4 (nand_4_out, xor_4_out, I0);
  nand nand_5 (nand_5_out, I1, nand_3_out);
  nand nand_6 (nand_6_out, nand_3_out, Fn);
  or or_4 (Function, and_3_out, and_4_out);
  nand nand_7 (Fout, nand_4_out, nand_5_out);
  nand nand_8 (Cout, nand_6_out, nand_6_out);

  // Other names for the same wires on the sheet: F = Fn

  // Notes on the sheet:
  //   OR
  //   AND
  //   XOR
  //   ADD
  //   3 chip (12 gate ) bit serial ALU
  //   Z80 single ALU bit
  //   Suppress Carry
endmodule
